# Fritzing sketch Sketch (saved by Fritzing 0.9.3b)
breadboards: 1

parts:
  U1 = ATTINY13 [package=dip]
  CONN1 = USB connector [package=THT]
  C2 = Electrolytic Capacitor [capacitance=10µF package="0405 [SMD, electrolytic]"]
  T1 = LM35 Temperature Sensor [package="TO92 [THT]"]
  C3 = Electrolytic Capacitor [capacitance=10µF package="0405 [SMD, electrolytic]"]
  T2 = LM35 Temperature Sensor [package="TO92 [THT]"]
  C4 = Electrolytic Capacitor [capacitance=10µF package="0405 [SMD, electrolytic]"]
  T3 = LM35 Temperature Sensor [package="TO92 [THT]"]
  C5 = Electrolytic Capacitor [capacitance=10µF package="0405 [SMD, electrolytic]"]

nets:
  N1: U1.PB3(ADC3), C4.+, T3.Vout
  N2: U1.PB4(ADC2), C3.+, T2.Vout
  GND: U1.GND, CONN1.GND, CONN1.chassis5, CONN1.chassis6, C2.-, T1.GND, C3.-, T2.GND, C4.-, T3.GND, C5.-
  N3: U1.PB0(MOSI), CONN1.d-
  N4: U1.PB1(MISO), CONN1.d+
  N5: U1.PB2(SCK_ADC1), C2.+, T1.Vout
  VCC: U1.VCC, CONN1.5V, T1.+Vs, T2.+Vs, T3.+Vs, C5.+
